# Fritzing sketch MQ3-Breathalyzer (saved by Fritzing 0.9.2b)
perfboards: 1

parts:
  Part1 = Arduino Nano (Rev3.0)
  U1 = GAS_SENSOR [package=mq-3]
  J1 = Piezo Speaker
  U2 = LCD-16X2 [package=lcd-16x2_noholes]
  LED1 = RGB LED (com. anode, rbg) [package="5 mm [THT]"]

nets:
  N1: Part1.D2, U2.DB7
  N2: Part1.D3, U2.DB6
  N3: Part1.D4, U2.DB5
  N4: Part1.D5, U2.DB4
  N5: Part1.D9, U2.RS
  N6: Part1.D10, LED1.green_cathode
  N7: Part1.D11/MOSI, LED1.blue_cathode
  N8: Part1.D12/MISO, LED1.red_cathode
  N9: Part1.5V, U1.H2
  N10: Part1.A1, J1.pin2
  N11: Part1.A0, U1.H1
