# Fritzing sketch motion_box_schematic (saved by Fritzing 0.9.2b)
breadboards: 1

parts:
  Part1 = Arduino Micro (Rev3)  # not connected
  U1 = RELAY-2 [package=relay-g5v]
  J1 = Screw terminal - 2 pins [package=THT]
  PIR1 = PIR sensor  # not connected
  VCC1 = Battery block 9V
  LED2 = LED - 5mm [color="Red (633nm)" package="5 mm [THT]"]
  R1 = Resistor [tolerance=±5% resistance=220 package=THT]
  LED1 = RGB LED - (4 legs) [package="5 mm [THT]"]

nets:
  N1: U1.1, U1.2
  N2: U1.6, J1.pin2
  N3: U1.9, U1.10
  N4: VCC1.-, LED2.anode
  N5: R1.Pin_0, LED1.common_anode
