# Fritzing sketch motion_box_schematic (saved by Fritzing 0.9.2b)
circuit board: 8.46667cm x 5.64444cm
perfboards: 1

parts:
  Part2 = Arduino Micro (Rev3)
  RGB_LED = RGB LED (com. anode, rbg) [package="5 mm [THT]"]
  Relay = RELAY-2 [part_number="5v coil with 120v contact rating" package=relay-g5v]
  power_terminal = Screw terminal - 2 pins [package=THT]
  PIR_Sensor = PIR sensor
  R1 = Resistor [tolerance=±5% resistance=220 package=THT]

nets:
  GND: Part2.GND, PIR_Sensor.GND, R1.Pin_1
  N1: Part2.D5_PWM, RGB_LED.green_cathode
  N2: Part2.D6_PWM/A7, RGB_LED.blue_cathode
  N3: Part2.D7, RGB_LED.red_cathode
  N4: Part2.D12_PWM/A11, Relay.1
  5V: Part2.5V, PIR_Sensor.VDD
  N5: Part2.D13_PWM, PIR_Sensor.SIG
  N6: RGB_LED.common_anode, R1.Pin_0
  N7: Relay.6, power_terminal.pin2
