# Fritzing sketch tea-dunker-schematic (saved by Fritzing 0.9.2b)
perfboards: 1

parts:
  Part1 = Arduino Nano (Rev3.0) (ICSP)
  micro_servo = Basic Servo
  ultrasonic_sensor = SRF05 Ultrasonic Rangefinder

nets:
  GND: Part1.GND, micro_servo.gnd, ultrasonic_sensor.GND
  5V: Part1.5V, ultrasonic_sensor.VCC
  N1: Part1.D13/SCK, micro_servo.pulse
